# Fritzing sketch led_onoff (saved by Fritzing 0.9.9b)
breadboards: 1

parts:
  Arduino_Uno = Arduino Uno (Rev3)
  R1 = Resistor [tolerance=±5% power=0.25 resistance=990 package=THT]
  LED1 = LED - 5mm [color="Red (633nm)" current=0.030 package="5 mm [THT]"]

nets:
  N1: Arduino_Uno.D13/SCK, R1.Pin_0
  N2: Arduino_Uno.5V, LED1.anode
  N3: R1.Pin_1, LED1.cathode
