# Fritzing sketch at328-0 (saved by Fritzing 0.9.9b)
breadboards: 1

parts:
  Part1 = Arduino Uno (Rev3)
  LED1 = LED - 3mm [color="Red (633nm)" current=0.030 package="3 mm [THT]"]
  R1 = Resistor [tolerance=±5% resistance=990 package="2512 [SMD]"]

nets (from the schematic view):
  N1: Part1.A0, LED1.anode
  N2: Part1.GND, R1.Pin_1
  N3: LED1.cathode, R1.Pin_0

// code stored in the sketch: at328-1.ino

