# Fritzing sketch at328-1 (saved by Fritzing 0.9.9b)
breadboards: 1

parts:
  Part1 = Arduino Uno (Rev3)
  LED1 = LED - 3mm [color="Red (633nm)" current=0.030 package="3 mm [THT]"]
  R1 = Resistor [tolerance=±5% resistance=330 package="2512 [SMD]"]
  S1 = Momentary Switch [package=tactile-pth]

nets:
  N1: Part1.A0, LED1.anode
  N2: Part1.A1, S1.3
  N3: Part1.GND, R1.Pin_1
  N4: LED1.cathode, R1.Pin_0, S1.1
